# Fritzing sketch sketch (saved by Fritzing 0.9.4)

parts:
  WeMos_D1_Mini1 = WeMos D1 Mini
  Bauteil1 = Logic Level Converter
  J1 = Dagu DGServo 9g header (male) [package=THT]
  TD-er1 = MH-Z19 CO2 sensor [part_number=MH-Z19]

nets:
  N1: WeMos_D1_Mini1.3V3, Bauteil1.LV
  5V: WeMos_D1_Mini1.5V, Bauteil1.HV, J1.Vcc, TD-er1.Vin
  N2: WeMos_D1_Mini1.D1, TD-er1.TX
  N3: WeMos_D1_Mini1.D2, TD-er1.RX
  N4: WeMos_D1_Mini1.D7, Bauteil1.TX2_LV
  GND: WeMos_D1_Mini1.G, Bauteil1.GND, J1.gnd, TD-er1.GND
  N5: Bauteil1.TX2_HV, J1.pulse
